# Fritzing sketch CopyPasteVolume (saved by Fritzing 0.9.3b)

parts:
  Pro_Micro1 = SparkFun Pro Micro
  S1 = Round Pushbutton
  S4 = Round Pushbutton  # not connected
  R1 = Rotary Potentiometer (Small) [maximum_resistance=100kΩ package=THT]

nets:
  N1: Pro_Micro1.GND, R1.leg1
  N2: Pro_Micro1.4, S1.leg0
  N3: Pro_Micro1.A3, R1.wiper
  N4: Pro_Micro1.VCC, R1.leg2

custom parts:
  SparkFun Pro Micro: The Pro Micro is similar to the Pro Mini except with an ATmega32U4 on board. The USB transceiver inside the 32U4 allows us to add USB connectivity on-board and do away with bulky external USB interface. Based on: https://github.com/unorthodox-engineers/unorthodox-arduino/blob/master/Unorthodox/fritzing/parts/Pro%20Micro.fzpz
